# Fritzing sketch circuit (saved by Fritzing 0.9.2b)

parts:
  Part1 = Arduino Uno (Rev3)
  R2 = Resistor [tolerance=±5% resistance=220 package=THT]
  R3 = Resistor [tolerance=±5% resistance=390 package=THT]
  R4 = Resistor [tolerance=±5% resistance=270 package=THT]
  R5 = Resistor [tolerance=±5% resistance=1k package=THT]
  LCD1 = LCD screen
  S1 = Pushbutton [package="[THT]"]
  S2 = Pushbutton [package="[THT]"]
  S3 = Pushbutton [package="[THT]"]
  KY-1 = Keyes Relay [package=THT]
  M1 = DC Motor
  Power_plug1 = Power plug
  F1 = FUSE [package=fuse_5mm]
  F2 = FUSE [package=fuse_5mm]
  U1 = DS1307 [package=so08]
  S4 = SWITCH-SPST-2 [package=switch-spst-vertical]

nets:
  N1: Part1.A0, R4.Pin_0, R5.Pin_1, S1.Pin_3, S1.Pin_4
  N2: Part1.D8, KY-1.signal
  N3: Part1.D13/SCK, LCD1.E
  GND: Part1.GND, LCD1.VSS, LCD1.V0, LCD1.RS, LCD1.R/W, LCD1.LED-, S1.Pin_1, S1.Pin_2, S2.Pin_1, S2.Pin_2, S3.Pin_2, KY-1.ground, M1.pin_2, Power_plug1.GND, U1.GND, S4.O
  N4: Part1.A4/SDA, U1.SDA
  N5: Part1.A5/SCL, U1.SCL
  N6: Part1.D2, U1.SQW
  N7: Part1.D3_PWM, S4.P
  N8: Part1.D4, LCD1.DB0
  N9: Part1.D5_PWM, LCD1.DB1
  N10: Part1.D6_PWM, LCD1.DB2
  N11: Part1.D7, LCD1.DB3
  5V: Part1.5V, R2.Pin_1, R5.Pin_0, LCD1.VDD, KY-1.power, U1.VCC
  N12: Part1.VIN, F1.2
  N13: R2.Pin_0, LCD1.LED+
  N14: R3.Pin_0, R4.Pin_1, S2.Pin_3, S2.Pin_4
  N15: R3.Pin_1, S3.Pin_3, S3.Pin_4
  N16: KY-1.C, F2.2
  N17: KY-1.NO, M1.pin_1
  N18: Power_plug1.VCC, F1.1, F2.1

custom parts:
  Keyes Relay: The Keyes 5V relay module is suitable for SCM development, home appliance control. It uses a 5V~12V TIL control signal which can control DC / AC signal.
